# Fritzing sketch PlanetWeightSound (saved by Fritzing 0.9.4)
circuit board: 5.9cm x 6.3cm
breadboards: 1

parts:
  DFRobot_DFPlayer_Mini1 = DFRobot DFPlayer Mini [part_number=DFR0299]
  VCC1 = 4 x AAA Battery Mount  # not connected
  SP1 = SPEAKER [package=pcb_mount_speaker]
  R1 = Resistor [tolerance=±5% resistance=10 package=THT]
  Speaker = female pin header, 3 pins [form="♀ (female)"]
  Arduino_Micro = Arduino Micro (Rev3)
  LED_0 = molex pin header, 5 pins [form=molex]
  LED_1 = molex pin header, 5 pins [form=molex]
  LED_2 = molex pin header, 5 pins [form=molex]
  LED_3 = molex pin header, 5 pins [form=molex]
  Power = female alternating pin header, 2 pins [form="♀ (female)"]
  Vol = Trimmer Potentiometer [maximum_resistance=100kΩ package=THT]
  Load_Cell = female pin header, 4 pins [form="♀ (female)"]

nets:
  VCC: DFRobot_DFPlayer_Mini1.VCC, Arduino_Micro.5V, LED_0.pin4, LED_0.pin5, LED_1.pin4, LED_1.pin5, LED_2.pin4, LED_2.pin5, LED_3.pin4, LED_3.pin5, Vol.leg2
  N1: DFRobot_DFPlayer_Mini1.RX, R1.Pin_1
  N2: DFRobot_DFPlayer_Mini1.TX, Arduino_Micro.D10_PWM/A10
  N3: DFRobot_DFPlayer_Mini1.SPK_1, Speaker.pin1
  N4: DFRobot_DFPlayer_Mini1.GND-1, DFRobot_DFPlayer_Mini1.GND-2, Speaker.pin2, Arduino_Micro.GND, LED_0.pin3, LED_1.pin3, LED_2.pin3, LED_3.pin3, Power.pin2, Vol.leg1, Load_Cell.pin4
  N5: DFRobot_DFPlayer_Mini1.SPK_2, SP1.+, Speaker.pin3
  N6: R1.Pin_0, Arduino_Micro.D11_PWM
  N7: Arduino_Micro.D2/SDA, LED_0.pin2, LED_1.pin2, LED_2.pin2, LED_3.pin2
  N8: Arduino_Micro.D3/SCL, LED_0.pin1, LED_1.pin1, LED_2.pin1, LED_3.pin1
  N9: Arduino_Micro.VIN, Power.pin1, Load_Cell.pin3
  N10: Arduino_Micro.A2, Vol.wiper
  N11: Arduino_Micro.A1, Load_Cell.pin2
  N12: Arduino_Micro.A0, Load_Cell.pin1
