# Fritzing sketch amplifier_board (saved by Fritzing 0.9.4)
circuit board: 5.4cm x 3.7968cm
breadboards: 1

parts:
  J1 = female pin header, 6 pins [form="♀ (female)"]
  J3 = female pin header, 4 pins [form="♀ (female)"]
  J4 = screw terminal, 4 pins
  J2 = screw terminal, 8 pins

nets:
  N1: J1.pin1, J2.pin6, J2.pin8
  N2: J1.pin2, J2.pin5, J2.pin7
  N3: J1.pin3, J2.pin4
  N4: J1.pin4, J2.pin3
  N5: J1.pin5, J2.pin2
  N6: J1.pin6, J2.pin1
  N7: J3.pin1, J4.pin1
  N8: J3.pin2, J4.pin2
  N9: J3.pin3, J4.pin3
  N10: J3.pin4, J4.pin4
